# Fritzing sketch SumoBot_Fritzing_Sketch (saved by Fritzing 0.9.10b)
breadboards: 1

parts:
  MH-ET_LIVE_ESP32_DEVKIT1 = MH-ET LIVE ESP32 DEVKIT 38 pins
  TCRT1 = TCRT5000 digital module [part_number=151608]
  TCRT2 = TCRT5000 digital module [part_number=151608]
  TCRT3 = TCRT5000 digital module [part_number=151608]
  TCRT4 = TCRT5000 digital module [part_number=151608]

nets:
  N1: MH-ET_LIVE_ESP32_DEVKIT1.IO34, TCRT2.DO1
  GND: MH-ET_LIVE_ESP32_DEVKIT1.GND#58, TCRT1.GND, TCRT2.GND
  N2: MH-ET_LIVE_ESP32_DEVKIT1.IO13, TCRT1.DO1
  VCC: MH-ET_LIVE_ESP32_DEVKIT1.5V, TCRT1.VCC, TCRT2.VCC, TCRT3.VCC, TCRT4.VCC
  GND_2: MH-ET_LIVE_ESP32_DEVKIT1.GND#64, TCRT3.GND, TCRT4.GND
  N3: MH-ET_LIVE_ESP32_DEVKIT1.IO23, TCRT4.DO1
  N4: MH-ET_LIVE_ESP32_DEVKIT1.IO4, TCRT3.DO1

custom parts:
  MH-ET LIVE ESP32 DEVKIT 38 pins: http://mh.nodebb.com/topic/2/mh-et-live-esp32-devkit
  TCRT5000 digital module: breakout board for TCRT5000 module, convert analog to digital - Uses TCRT5000 infrared reflectance sensor - Detection distance: 1mm~8mm - Focus distance: 2.5mm - Working voltage: 3.3V~12V - Uses wide voltage LM393 comparator - With multi-turn precision potentiometer to adjust the sensitivity - Current: > 15mA - Output type: Digital switch output (0, 1) - Suitable for watt-hour meter pulse data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
